# Fritzing sketch Lesson203v2 (saved by Fritzing 0.9.3b)
breadboards: 1

parts:
  Part1 = Adafruit BME280
  Raspberry_Pi_1 = Raspberry Pi 3 [part_number=RPI-3-V1.2]

nets:
  VIN: Part1.VIN, Raspberry_Pi_1.5V
  GND: Part1.GND, Raspberry_Pi_1.GND
  N1: Part1.SCK/SCL, Raspberry_Pi_1.GPIO3
  N2: Part1.SDI/SDA, Raspberry_Pi_1.GPIO2

custom parts:
  Adafruit BME280: Bosch has stepped up their game with their new BME280 sensor, an environmental sensor with temperature, barometric pressure and humidity! This sensor is great for all sorts of weather/environmental sensing and can even be used in both I2C and SPI! This precision sensor from Bosch is the best low-cost sensing solution for measuring humidity with ±3% accuracy, barometric pressure with ±1 hPa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
